# Fritzing sketch LyncDisplayLight_Wiring (saved by Fritzing 0.9.3b)

parts:
  WeMos_D1_Mini3 = WeMos D1 Mini
  WeMos_D1_Mini_WS2812B_RGB_Shield2 = WeMos D1 Mini WS2812B RGB Shield
  OLED_I2C1 = OLED 128x64 I2C Monochrome Display

nets:
  5V: WeMos_D1_Mini3.5V, WeMos_D1_Mini_WS2812B_RGB_Shield2.5V, OLED_I2C1.VDD
  N1: WeMos_D1_Mini3.D2, WeMos_D1_Mini_WS2812B_RGB_Shield2.D2
  N2: WeMos_D1_Mini3.D3, OLED_I2C1.SDA
  N3: WeMos_D1_Mini3.D4, OLED_I2C1.SCK
  N4: WeMos_D1_Mini3.G, WeMos_D1_Mini_WS2812B_RGB_Shield2.G, OLED_I2C1.GND
